// Logisim project hw5pr1.circ as structural Verilog
module MyXOR (
  input  X,
  input  X_2,
  output out_3
);

  wire and_1_out, and_2_out, not_1_out, not_2_out;

  not not_1 (not_1_out, X);
  not not_2 (not_2_out, X_2);
  and and_1 (and_1_out, not_1_out, X_2);
  and and_2 (and_2_out, X, not_2_out);
  or or_1 (out_3, and_1_out, and_2_out);

  // Notes on the sheet:
  //   hw5pr1
  //   Lab Instructor: Meng
  //   Lab Time: Tuesday 8-10
  //   Names: Bhagawat Acharya and Vincent Minocci
  //   XOR Circuit built using Logisim
endmodule

module FullAdder (
  input  X,
  input  Y,
  input  CarryIn,
  output sum,
  output CarryOut
);

  wire and_1_out, and_2_out, and_3_out, and_4_out, and_5_out, and_6_out, and_7_out, and_8_out, not_1_out,
       not_2_out, not_3_out, not_4_out, not_5_out, not_6_out, not_7_out, or_1_out;

  and and_1 (and_1_out, X, Y, CarryIn);
  not not_1 (not_1_out, Y);
  not not_2 (not_2_out, X);
  and and_2 (and_2_out, X, not_1_out);
  and and_3 (and_3_out, not_2_out, Y);
  or or_1 (or_1_out, and_2_out, and_3_out);
  not not_3 (not_3_out, X);
  and and_4 (and_4_out, not_3_out, Y, CarryIn);
  not not_4 (not_4_out, Y);
  and and_5 (and_5_out, X, not_4_out, CarryIn);
  or or_2 (CarryOut, and_1_out, and_4_out, and_5_out, and_6_out);
  not not_5 (not_5_out, CarryIn);
  not not_6 (not_6_out, or_1_out);
  and and_6 (and_6_out, X, Y, not_7_out);
  and and_7 (and_7_out, or_1_out, not_5_out);
  and and_8 (and_8_out, not_6_out, CarryIn);
  not not_7 (not_7_out, CarryIn);
  or or_3 (sum, and_7_out, and_8_out);

  // Notes on the sheet:
  //   This adds two one digit binary numbers
endmodule

module _4_bit_Ripple_Carry_Adder (
  input  Y3,
  input  Y2,
  input  Y1,
  input  Y0,
  input  X3,
  input  X2,
  input  X1,
  input  X0,
  output Sum4,
  output Sum3,
  output Sum2,
  output Sum1,
  output Sum0
);

  wire fulladder_1_p3, fulladder_2_p3, fulladder_3_p3;

  // hw5pr1_FullAdder fulladder_1: pin names not known; wires that end beside it: Y3, X3, fulladder_1_p3, Sum3, Sum4
  // hw5pr1_FullAdder fulladder_2: pin names not known; wires that end beside it: Y2, X2, fulladder_2_p3, Sum2, fulladder_1_p3
  // hw5pr1_FullAdder fulladder_3: pin names not known; wires that end beside it: Y1, X1, fulladder_3_p3, Sum1, fulladder_2_p3
  // hw5pr1_FullAdder fulladder_4: pin names not known; wires that end beside it: 1'b0, Y0, X0, Sum0, fulladder_3_p3

  // Notes on the sheet:
  //   This adds two 4 digit binary numbers
endmodule

module _4_bit_Multiplier (
  input  Y3,
  input  Y2,
  input  Y1,
  input  Y0,
  input  X3,
  input  X2,
  input  X1,
  input  X0,
  output Z7,
  output Z6,
  output Z5,
  output Z4,
  output Z3,
  output Z2,
  output Z1,
  output Z0
);

  wire n4x1_multiplier_1_z0, n4x1_multiplier_1_z1, n4x1_multiplier_1_z2, n4x1_multiplier_1_z3,
       n4x1_multiplier_2_z0, n4x1_multiplier_2_z1, n4x1_multiplier_2_z2, n4x1_multiplier_2_z3,
       n4x1_multiplier_3_z0, n4x1_multiplier_3_z1, n4x1_multiplier_3_z2, n4x1_multiplier_3_z3,
       n4x1_multiplier_4_z0, n4x1_multiplier_4_z1, n4x1_multiplier_4_z2, n4x1_multiplier_4_z3;

  _4x1_Multiplier u_4x1_multiplier_1 (
    .X0(X3), .Y3(Y3), .Y2(Y2), .Y1(Y1), .Y0(Y0), .Z3(n4x1_multiplier_1_z3), .Z2(n4x1_multiplier_1_z2),
    .Z1(n4x1_multiplier_1_z1), .Z0(n4x1_multiplier_1_z0));
  _4x1_Multiplier u_4x1_multiplier_2 (
    .X0(X2), .Y3(Y3), .Y2(Y2), .Y1(Y1), .Y0(Y0), .Z3(n4x1_multiplier_2_z3), .Z2(n4x1_multiplier_2_z2),
    .Z1(n4x1_multiplier_2_z1), .Z0(n4x1_multiplier_2_z0));
  _4x1_Multiplier u_4x1_multiplier_3 (
    .X0(X1), .Y3(Y3), .Y2(Y2), .Y1(Y1), .Y0(Y0), .Z3(n4x1_multiplier_3_z3), .Z2(n4x1_multiplier_3_z2),
    .Z1(n4x1_multiplier_3_z1), .Z0(n4x1_multiplier_3_z0));
  _4x1_Multiplier u_4x1_multiplier_4 (
    .X0(X0), .Y3(Y3), .Y2(Y2), .Y1(Y1), .Y0(Y0), .Z3(n4x1_multiplier_4_z3), .Z2(n4x1_multiplier_4_z2),
    .Z1(n4x1_multiplier_4_z1), .Z0(n4x1_multiplier_4_z0));
  _4_bit_Ripple_Carry_Adder u_4_bit_ripple_carry_adder_1 (.X0(n4x1_multiplier_4_z0));  // open: Y3, X3, Y2, X2, Y1, X1, Y0, Sum4, Sum3, Sum2, Sum1, Sum0

  // Notes on the sheet:
  //   factor (4 bits)
  //   See the problem for details on this hint: perhaps build a 4x1-bit multiplier first!
  //   second factor (4 bits)
  //   most significant (highest) bit
  //   least significant (lowest) bit
  //   product (7 bits)
endmodule

module _3by2_divider (
  input  Y2,
  input  Y1,
  input  Y0,
  input  X1,
  input  X0,
  output Z2,
  output Z1,
  output Z0,
  output Error
);


  // Notes on the sheet:
  //   Dividend (3 bits: Y2 Y1 Y0)
  //   Divisor (2 bits: X1 X0)
  //   Quotient (4 bits: Z2 Z1 Z0 and Error)
endmodule

module _4x1_Multiplier (
  input  Y3,
  input  Y2,
  input  Y1,
  input  Y0,
  input  X0,
  output Z3,
  output Z2,
  output Z1,
  output Z0
);

  and and_1 (Z3, X0, Y3);
  and and_2 (Z2, X0, Y2);
  and and_3 (Z1, X0, Y1);
  and and_4 (Z0, X0, Y0);
endmodule
